// Logisim project projeto de circuto.circ as structural Verilog: 13 circuits, main circuit 1Segmento
module Main (
  input  in_1,
  input  Jogador_0,
  input  in_3,
  input  in_4,
  input  Jogar,
  input  in_6,
  input  in_7,
  input  in_8,
  input  in_9,
  input  Jogador,
  output Maior,
  output Acertou,
  output Menor
);

  wire display_1_out_5, display_1_out_6, display_1_out_7, display_1_out_8, display_1_out_9, display_1_out_10,
       display_1_out_11, display_2_out_5, display_2_out_6, display_2_out_7, display_2_out_8, display_2_out_9,
       display_2_out_10, display_2_out_11;

  _7_Segment_Display u_7_segment_display_1 (
    .g(display_1_out_11), .f(display_1_out_9), .a(display_1_out_10), .b(display_1_out_5),
    .e(display_1_out_8), .d(display_1_out_7), .c(display_1_out_6));  // open: dp
  _7_Segment_Display u_7_segment_display_2 (
    .g(display_2_out_11), .f(display_2_out_9), .a(display_2_out_10), .b(display_2_out_5),
    .e(display_2_out_8), .d(display_2_out_7), .c(display_2_out_6));  // open: dp
  Display display_1 (
    .A(in_1), .B(Jogador_0), .C(in_3), .D(in_4), .out_5(display_1_out_5), .out_6(display_1_out_6),
    .out_7(display_1_out_7), .out_8(display_1_out_8), .out_9(display_1_out_9), .out_10(display_1_out_10),
    .out_11(display_1_out_11));
  Display display_2 (
    .A(in_6), .B(in_7), .C(in_8), .D(in_9), .out_5(display_2_out_5), .out_6(display_2_out_6),
    .out_7(display_2_out_7), .out_8(display_2_out_8), .out_9(display_2_out_9), .out_10(display_2_out_10),
    .out_11(display_2_out_11));
  Multiplexador multiplexador_1 (
    .Jogando(Jogar), .A({in_1, Jogador_0, in_3, in_4}), .B({in_6, in_7, in_8, in_9}), .S(Jogador),
    .Maior(Maior), .Igual(Acertou), .Menor(Menor));

  // Notes on the sheet:
  //   Jogador 1
endmodule

module Multiplexador (
  input  Jogando,
  input  [3:0] A,
  input  [3:0] B,
  input  S,
  output Maior,
  output Igual,
  output Menor
);

  wire \operações_1_iqual , \operações_1_maior , \operações_1_menor ;
  wire [3:0] mux_1_out_4;

  Mux mux_1 (.in_3(S), .out_4(mux_1_out_4), .in_1(A), .in_2(B));
  \Operações  \operações_1  (
    .Iqual(\operações_1_iqual ), .Menor(\operações_1_menor ), .Maior(\operações_1_maior ),
    .in_1(mux_1_out_4), .in_2(4'b1001));
  and and_1 (Maior, \operações_1_maior , Jogando);
  and and_2 (Igual, \operações_1_iqual , Jogando);
  and and_3 (Menor, \operações_1_menor , Jogando);
endmodule

module _1Segmento (
  input  A,
  input  B,
  input  C,
  input  D,
  output out_5
);

  wire and_1_out, and_2_out, and_3_out, and_4_out, and_5_out, not_1_out, not_2_out, not_3_out, not_4_out,
       not_5_out, not_6_out, not_7_out, not_8_out, not_9_out;

  not not_1 (not_1_out, A);
  not not_2 (not_2_out, B);
  not not_3 (not_3_out, C);
  not not_4 (not_4_out, D);
  not not_5 (not_5_out, A);
  not not_6 (not_6_out, A);
  not not_7 (not_7_out, C);
  not not_8 (not_8_out, B);
  not not_9 (not_9_out, D);
  and and_1 (and_1_out, not_1_out, not_2_out);
  and and_2 (and_2_out, not_3_out, not_4_out, not_5_out);
  and and_3 (and_3_out, C, D, not_6_out);
  and and_4 (and_4_out, not_7_out, A, D);
  and and_5 (and_5_out, not_8_out, not_9_out);
  or or_1 (out_5, and_1_out, and_2_out, and_3_out, and_4_out, and_5_out);
endmodule

module _2Segmento (
  input  A,
  input  B,
  input  C,
  input  D,
  output out_5
);

  wire and_1_out, and_2_out, and_3_out, and_4_out, and_5_out, not_1_out, not_2_out, not_3_out, not_4_out,
       not_5_out, not_6_out;

  not not_1 (not_1_out, A);
  not not_2 (not_2_out, C);
  not not_3 (not_3_out, C);
  not not_4 (not_4_out, B);
  not not_5 (not_5_out, B);
  not not_6 (not_6_out, A);
  and and_1 (and_1_out, not_1_out, not_2_out);
  and and_2 (and_2_out, not_3_out, D);
  and and_3 (and_3_out, not_4_out, D);
  and and_4 (and_4_out, A, not_5_out);
  and and_5 (and_5_out, B, not_6_out);
  or or_1 (out_5, and_1_out, and_2_out, and_3_out, and_4_out, and_5_out);
endmodule

module _3Segmento (
  input  A,
  input  B,
  input  C,
  input  D,
  output out_5
);

  wire and_1_out, and_2_out, and_3_out, and_4_out, and_5_out, and_6_out, not_1_out, not_2_out, not_3_out,
       not_4_out, not_5_out, not_6_out, not_7_out, not_8_out, not_9_out;

  not not_1 (not_1_out, C);
  not not_2 (not_2_out, C);
  not not_3 (not_3_out, B);
  not not_4 (not_4_out, A);
  not not_5 (not_5_out, B);
  not not_6 (not_6_out, D);
  not not_7 (not_7_out, A);
  not not_8 (not_8_out, B);
  not not_9 (not_9_out, D);
  and and_1 (and_1_out, A, not_1_out);
  and and_2 (and_2_out, B, D, not_2_out);
  and and_3 (and_3_out, A, D, not_3_out);
  and and_4 (and_4_out, C, not_4_out, not_5_out);
  and and_5 (and_5_out, C, not_6_out, B);
  and and_6 (and_6_out, not_7_out, not_8_out, not_9_out);
  or or_1 (out_5, and_1_out, and_2_out, and_3_out, and_4_out, and_5_out, and_6_out);
endmodule

module _4Segmento (
  input  A,
  input  B,
  input  C,
  input  D,
  output out_5
);

  wire and_1_out, and_2_out, and_3_out, and_4_out, not_1_out, not_2_out, not_3_out, not_4_out;

  not not_1 (not_1_out, B);
  not not_2 (not_2_out, D);
  not not_3 (not_3_out, A);
  not not_4 (not_4_out, D);
  and and_1 (and_1_out, not_1_out, not_2_out);
  and and_2 (and_2_out, A, B);
  and and_3 (and_3_out, A, C);
  and and_4 (and_4_out, not_3_out, C, not_4_out);
  or or_1 (out_5, and_1_out, and_2_out, and_3_out, and_4_out);
endmodule

module _5segmento (
  input  A,
  input  B,
  input  C,
  input  D,
  output out_5
);

  wire and_1_out, and_2_out, and_3_out, and_4_out, and_5_out, not_1_out, not_2_out, not_3_out, not_4_out,
       not_5_out, not_6_out;

  not not_1 (not_1_out, D);
  and and_1 (and_1_out, not_1_out, not_2_out);
  not not_2 (not_2_out, C);
  and and_2 (and_2_out, A, not_3_out);
  not not_3 (not_3_out, B);
  not not_4 (not_4_out, A);
  and and_3 (and_3_out, not_4_out, B, not_5_out);
  not not_5 (not_5_out, C);
  and and_4 (and_4_out, A, B, C);
  and and_5 (and_5_out, B, C, not_6_out);
  not not_6 (not_6_out, D);
  or or_1 (out_5, and_1_out, and_2_out, and_3_out, and_4_out, and_5_out);
endmodule

module _6Segmento (
  input  A,
  input  B,
  input  C,
  input  D,
  output out_5
);

  wire and_1_out, and_2_out, and_3_out, and_4_out, and_5_out, and_6_out, and_7_out, not_1_out, not_2_out,
       not_3_out, not_4_out, not_5_out, not_6_out, not_7_out, not_8_out, not_9_out, not_10_out;

  not not_1 (not_1_out, D);
  not not_2 (not_2_out, A);
  not not_3 (not_3_out, B);
  not not_4 (not_4_out, C);
  not not_5 (not_5_out, D);
  not not_6 (not_6_out, A);
  not not_7 (not_7_out, C);
  not not_8 (not_8_out, D);
  not not_9 (not_9_out, B);
  not not_10 (not_10_out, C);
  and and_1 (and_1_out, C, not_1_out);
  and and_2 (and_2_out, C, not_2_out);
  and and_3 (and_3_out, not_3_out, not_4_out, not_5_out);
  and and_4 (and_4_out, not_6_out, B, D);
  and and_5 (and_5_out, A, B, C);
  and and_6 (and_6_out, A, not_7_out, not_8_out);
  and and_7 (and_7_out, A, not_9_out, not_10_out);
  or or_1 (out_5, and_1_out, and_2_out, and_3_out, and_4_out, and_5_out, and_6_out, and_7_out);
endmodule

module _7Segmento (
  input  A,
  input  B,
  input  C,
  input  D,
  output out_5
);

  wire and_1_out, and_2_out, and_3_out, and_4_out, and_5_out, not_1_out, not_2_out, not_3_out, not_4_out,
       not_5_out, not_6_out;

  not not_1 (not_1_out, B);
  not not_2 (not_2_out, D);
  not not_3 (not_3_out, A);
  not not_4 (not_4_out, B);
  not not_5 (not_5_out, A);
  not not_6 (not_6_out, C);
  and and_1 (and_1_out, A, not_1_out);
  and and_2 (and_2_out, C, not_2_out);
  and and_3 (and_3_out, not_3_out, not_4_out, C);
  and and_4 (and_4_out, not_5_out, B, not_6_out);
  and and_5 (and_5_out, A, B, D);
  or or_1 (out_5, and_1_out, and_2_out, and_3_out, and_4_out, and_5_out);
endmodule

module Display (
  input  A,
  input  B,
  input  C,
  input  D,
  output out_5,
  output out_6,
  output out_7,
  output out_8,
  output out_9,
  output out_10,
  output out_11
);

  _1Segmento _1 (.A(A), .B(B), .C(C), .D(D), .out_5(out_5));
  _2Segmento _2 (.A(A), .B(B), .C(C), .D(D), .out_5(out_6));
  _3Segmento _3 (.A(A), .B(B), .C(C), .D(D), .out_5(out_7));
  _4Segmento _4 (.A(A), .B(B), .C(C), .D(D), .out_5(out_8));
  _5segmento _5 (.A(A), .B(B), .C(C), .D(D), .out_5(out_9));
  _6Segmento _6 (.A(A), .B(B), .C(C), .D(D), .out_5(out_10));
  _7Segmento _7 (.A(A), .B(B), .C(C), .D(D), .out_5(out_11));
endmodule

module Mux (
  input  [3:0] in_1,
  input  [3:0] in_2,
  input  in_3,
  output [3:0] out_4
);

  Mux_1bit mux_1bit_1 (.out_4(out_4[0]), .A(in_1[0]), .B(in_2[0]), .S(in_3));
  Mux_1bit mux_1bit_2 (.out_4(out_4[1]), .A(in_1[1]), .B(in_2[1]), .S(in_3));
  Mux_1bit mux_1bit_3 (.out_4(out_4[2]), .A(in_1[2]), .B(in_2[2]), .S(in_3));
  Mux_1bit mux_1bit_4 (.out_4(out_4[3]), .A(in_1[3]), .B(in_2[3]), .S(in_3));
endmodule

module Mux_1bit (
  input  A,
  input  B,
  input  S,
  output out_4
);

  wire and_1_out, and_2_out, and_3_out, and_4_out;

  and and_1 (and_1_out, S, B, ~A);  // AND_Gate
  and and_2 (and_2_out, A, ~B, ~S);  // AND_Gate
  and and_3 (and_3_out, A, B, ~S);  // AND_Gate
  and and_4 (and_4_out, A, B, S);
  or or_1 (out_4, and_1_out, and_2_out, and_3_out, and_4_out);
endmodule

module \Operações  (
  input  [3:0] in_1,
  input  [3:0] in_2,
  output Iqual,
  output Menor,
  output Maior
);

  wire and_2_out, and_3_out, and_4_out, and_5_out, not_1_out, not_2_out, not_3_out, not_4_out, or_2_out,
       xnor_1_out, xnor_2_out, xnor_3_out, xnor_4_out;

  not not_1 (not_1_out, in_2[3]);
  not not_2 (not_2_out, in_2[2]);
  not not_3 (not_3_out, in_2[1]);
  not not_4 (not_4_out, in_2[0]);
  xnor xnor_1 (xnor_1_out, in_1[3], in_2[3]);
  xnor xnor_2 (xnor_2_out, in_1[2], in_2[2]);
  xnor xnor_3 (xnor_3_out, in_1[1], in_2[1]);
  xnor xnor_4 (xnor_4_out, in_1[0], in_2[0]);
  and and_1 (Iqual, xnor_1_out, xnor_2_out, xnor_3_out, xnor_4_out);
  and and_2 (and_2_out, in_1[3], not_1_out);
  and and_3 (and_3_out, xnor_1_out, in_1[2], not_2_out);
  and and_4 (and_4_out, xnor_2_out, xnor_1_out, in_1[1], not_3_out);
  and and_5 (and_5_out, xnor_1_out, xnor_2_out, xnor_3_out, in_1[0], not_4_out);
  or or_1 (Maior, and_2_out, and_3_out, and_4_out, and_5_out);
  or or_2 (or_2_out, Iqual, Maior);
  not not_5 (Menor, or_2_out);
endmodule
